# Fritzing sketch Contrl box wiring (saved by Fritzing 0.9.3b)
breadboards: 1

parts:
  Raspberry_Pi_1 = Raspberry Pi 3 [part_number=RPI-3-V1.2]
  External_Humidity_and_Temp = DHT11 Humitidy and Temperature Sensor [part_number="External Temp and Humidity Switch"]
  pH_Sensor = pH Circuit
  EC_sensor = Conductivity Circuit
  Water_Temp_sensor = DS18B20 1-Wire Temperature Sensor [part_number=DS18B20]
  Solution_A_pump = DC Motor [part_number="Solution B"]
  pH_Acid_pump = DC Motor
  motorcontrollerDRI1 = motorcontrollerDRI0002 [part_number="Nutrient solution motor controller"]
  Solution_B_pump = DC Motor
  12V_Power_Supply = LIPO-2000mAh [package=lipo-2000]
  Part2 = Arduino Uno (Rev3)
  motorcontrollerDRI2 = motorcontrollerDRI0002
  Valve_Solenoid = RelayModule DFR0017 [part_number="Solenoid Switch"]
  Float_Switch = SWITCH_SPDT [part_number="Float Switch" package=kps-1290]
  Sprinkler_System = RelayModule DFR0017 [part_number="Solenoid Switch"]
  Flow_meter = FLO-30 Circuit

nets:
  N1: Raspberry_Pi_1.GND, Raspberry_Pi_1.GPIO15, External_Humidity_and_Temp.NULL
  N2: Raspberry_Pi_1.GPIO17, Raspberry_Pi_1.GPIO18, External_Humidity_and_Temp.VDD
  N3: Raspberry_Pi_1.5V, External_Humidity_and_Temp.DATA
  VCC: pH_Sensor.Vcc, EC_sensor.Vcc, Water_Temp_sensor.VDD, motorcontrollerDRI1.VS, Part2.5V, motorcontrollerDRI2.VS, Valve_Solenoid.5V, Sprinkler_System.5V, Flow_meter.Vcc
  N4: pH_Sensor.PRB, Part2.A0
  GND: pH_Sensor.GND, EC_sensor.GND, Water_Temp_sensor.GND, motorcontrollerDRI1.GND, 12V_Power_Supply.-, Part2.GND, motorcontrollerDRI2.GND, Float_Switch.P, Flow_meter.GND
  N5: EC_sensor.PRB, Part2.A1
  N6: Water_Temp_sensor.DQ, Part2.A2
  N7: Solution_A_pump.pin_1, motorcontrollerDRI1.M1+
  N8: Solution_A_pump.pin_2, motorcontrollerDRI1.M1-
  N9: pH_Acid_pump.pin_1, motorcontrollerDRI2.M1-
  N10: pH_Acid_pump.pin_2, motorcontrollerDRI2.M1+
  N11: motorcontrollerDRI1.VD, 12V_Power_Supply.+, motorcontrollerDRI2.VD
  N12: motorcontrollerDRI1.E2, Part2.D4
  N13: motorcontrollerDRI1.M2, Part2.D5_PWM
  N14: motorcontrollerDRI1.M1, Part2.D3_PWM
  N15: motorcontrollerDRI1.E1, Part2.D2
  N16: motorcontrollerDRI1.M2+, Solution_B_pump.pin_2
  N17: motorcontrollerDRI1.M2-, Solution_B_pump.pin_1
  N18: Part2.A3, Flow_meter.PRB
  N19: Part2.D8, Valve_Solenoid.Input
  N20: Part2.D9_PWM, Sprinkler_System.Input
  N21: Part2.D12/MISO, Float_Switch.S
  N22: Part2.D6_PWM, motorcontrollerDRI2.M1
  N23: Part2.D7, motorcontrollerDRI2.E1

custom parts:
  DHT11 Humitidy and Temperature Sensor: DHT11 Humidity and Temperature Sensor
